# Fritzing sketch lightTheremin (saved by Fritzing 0.9.0b)
breadboards: 1

parts:
  R1 = Photocell (LDR) [package=THT]
  R2 = Resistor [tolerance=±5% resistance=10k package=THT]
  J1 = Piezo Speaker
  Bauteil1 = Arduino Uno (Rev3)

nets:
  N1: R1.pin_0, R2.Pin_1, Bauteil1.5V
  N2: R1.pin_1, R2.Pin_0, Bauteil1.A0
  N3: J1.pin1, Bauteil1.GND
  N4: J1.pin2, Bauteil1.D9_PWM

notes:
  see this video http://www.youtube.com/watch?v=57S3dylfw3I
