# Fritzing sketch light_dependend_resistor (saved by Fritzing 0.8.5b)
breadboards: 1

parts:
  R1 = Photocell (LDR) [package=THT]
  R2 = Resistor [tolerance=±5% resistance=10k package=THT]
  Bauteil1 = Arduino Uno (Rev3)

nets:
  N1: R1.pin_0, Bauteil1.5V
  N2: R1.pin_1, R2.Pin_0, Bauteil1.A0
  N3: R2.Pin_1, Bauteil1.GND

notes:
  //wikipedia: http://en.wikipedia.org/wiki/Photoresistor --> A photoresistor or light-dependent resistor (LDR) or photocell is a resistor whose resistance decreases with increasing incident light intensity; in other words, it exhibits photoconductivity.
  // http://bildr.org/2012/11/photoresistor-arduino/
  int LDR_Pin = A0; //analog pin 0
  void setup(){
  Serial.begin(9600);
  }
  void loop(){
  int LDRReading = analogRead(LDR_Pin);
  Serial.println(LDRReading);
  delay(250); //just here to slow down the output for easier reading
  }
