# Fritzing sketch pulse_width_modulation (saved by Fritzing 0.9.0b)
breadboards: 1

parts:
  LED1 = LED - 5mm [color="Red (633nm)" package="5 mm [THT]"]
  R2 = Resistor [tolerance=±5% resistance=220 package=THT]
  R1 = Rotary Potentiometer (Small) [maximum_resistance=10kΩ package=THT]
  Bauteil1 = Arduino Uno (Rev3)

nets:
  N1: LED1.cathode, R1.leg2, Bauteil1.GND
  N2: LED1.anode, R2.Pin_0
  N3: R2.Pin_1, Bauteil1.D9_PWM
  N4: R1.leg1, Bauteil1.5V
  N5: R1.wiper, Bauteil1.A0
