# Fritzing sketch temperature_AREF (saved by Fritzing 0.8.5b)
breadboards: 1

parts:
  T1 = TMP36 Temperature Sensor [package="TO92 [THT]"]
  Bauteil1 = Arduino Uno (Rev3)

nets:
  N1: T1.+Vs, Bauteil1.AREF, Bauteil1.3V3
  N2: T1.Vout, Bauteil1.A0
  GND: T1.GND, Bauteil1.GND
